# Fritzing sketch raspberrypiweatherstation (saved by Fritzing 0.9.3b)
circuit board: 8.46667cm x 5.64444cm

parts:
  Raspberry_Pi1 = Raspberry Pi B+
  U5 = SUP500F [package=sup500f]
  IC1 = MCP3008 8-channel 10-bit ADC [part_number=MCP3008]
  R11 = PHOTOCELL [package=photocell]
  Part1 = Adafruit BMP183
  DS1 = DS18B20 1-Wire Temperature Sensor [part_number=DS18B20]
  R12 = Resistor [tolerance=±5% resistance=4.7k package=THT]
  R14 = Resistor [tolerance=±5% resistance=10k package=THT]  # not connected
  R13 = Resistor [tolerance=±5% resistance=10k package=THT]  # not connected
  J1 = RJ11 Jack [package=rj11-6]  # not connected
  J2 = RJ11 Jack [package=rj11-6]  # not connected
  J3 = RJ11 Jack [package=rj11-6]  # not connected

nets (from the schematic view):
  3V3: Raspberry_Pi1.3v3, Raspberry_Pi1.3V3, IC1.no_name_yet#15, IC1.no_name_yet#16, R11.P$1, DS1.VDD, R12.Pin_1
  N1: Raspberry_Pi1.GPIO4, DS1.DQ, R12.Pin_0
  GND: Raspberry_Pi1.GND, U5.GND, IC1.no_name_yet#9, IC1.no_name_yet#14, Part1.GND, DS1.GND
  N2: Raspberry_Pi1.GPIO17, Part1.SCK
  N3: Raspberry_Pi1.GPIO27, Part1.CS
  N4: Raspberry_Pi1.GPIO22, Part1.SDO
  N5: Raspberry_Pi1.GPIO10, IC1.no_name_yet#11
  N6: Raspberry_Pi1.GPIO9, IC1.no_name_yet#12
  N7: Raspberry_Pi1.GPIO11, IC1.no_name_yet#13
  N8: Raspberry_Pi1.GPIO8, IC1.no_name_yet#10
  N9: Raspberry_Pi1.GPIO23, Part1.SDI
  N10: Raspberry_Pi1.GPIO15, U5.TX-O
  5V: Raspberry_Pi1.5V, U5.PSEL, Part1.VIN

custom parts:
  Adafruit BMP183: Fans of the BMP085/BMP180 will want to take a look at the new BMP183 - an SPI spin on the old familiar classic. This precision sensor from Bosch is the best low-cost sensing solution for measuring barometric pressure and temperature. Because pressure changes with altitude you can also use it as an altimeter! The BMP183 is the next-generation of sensors from Bosch, and is the fraternal twin of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
